# Fritzing sketch BoeDuinoBot (saved by Fritzing 0.6.3b)
breadboards: 1

parts:
  Netduino1 = Netduino
  J1 = female pin header, 3 pins [form="♂ (male)"]
  J2 = female pin header, 3 pins [form="♂ (male)"]
  S1 = Pushbutton [package="[THT]"]
  S2 = Pushbutton [package="[THT]"]
  R1 = TSR-3386UT Square Trimming Potentiometer [part_number=TSR-3386]
  R2 = TSR-3386UT Square Trimming Potentiometer [part_number=TSR-3386]
  U1 = Voltage Regulator - 5V [package="TO220 [THT]"]
  J3 = female pin header, 3 pins [form="♂ (male)"]
  J4 = female pin header, 3 pins [form="♂ (male)"]

nets:
  GND: Netduino1.GND, J1.pin1, J2.pin1, S1.Pin_3, S1.Pin_4, S2.Pin_3, S2.Pin_4, R1.Leg1, R2.Leg1, U1.GND
  N1: Netduino1.D10_PWM3, J4.pin2
  N2: Netduino1.D9_PWM2, J3.pin2
  N3: Netduino1.D6_PWM1, J2.pin2
  N4: Netduino1.D5_PWM0, J1.pin2
  N5: Netduino1.D0_RX0, S2.Pin_1, S2.Pin_2
  N6: Netduino1.RST, S1.Pin_1, S1.Pin_2
  N7: Netduino1.3V3, R1.Leg2, R2.Leg2
  N8: Netduino1.VIN, U1.input_voltage
  N9: Netduino1.A0, R1.wiper
  N10: Netduino1.A1, R2.wiper
  N11: J1.pin3, J2.pin3, U1.output_voltage, J3.pin3, J4.pin3
  N12: J3.pin1, J4.pin1

custom parts:
  TSR-3386UT Square Trimming Potentiometer: Trimpot 10K with Knob
